# Fritzing sketch stradivario (saved by Fritzing 0.9.2b)
breadboards: 1

parts:
  LiPo_Battery_750mAh_3_7V = LIPO-1000mAh [package=lipo-1000]
  LiPo_USB_Charger = USB LiPoly Charger
  RTC_Module = Real Time Clock Module - DS1307 RTC Breakout Board
  Mini_Slide_Switch = Toggle Switch [package=THT]
  DC-DC_Converter_3_7V-5V = NCP1400 Step-Up Breakout
  Rotary_Encoder = Rotary Encoder with Knob
  MS5611_Barometric_Pressure_Sensor = MS5611
  part = Resistor [tolerance=±5% resistance=100 package=THT]
  part_2 = Resistor [tolerance=±5% resistance=10k package=THT]
  R1 = Resistor [tolerance=±5% resistance=10k package=THT]
  part_3 = Resistor [tolerance=±5% resistance=10k package=THT]
  Arduino_Nano_V3_0 = Arduino Nano (Rev3.0)
  Buzzer_8_ohm = Piezo Speaker
  Nokia_5110_LCD_Module = Nokia 5110 LCD basado en PCD8544

nets:
  N1: LiPo_Battery_750mAh_3_7V.+, LiPo_USB_Charger.VBAT, Mini_Slide_Switch.L2
  GND: LiPo_Battery_750mAh_3_7V.-, LiPo_USB_Charger.GND, RTC_Module.GND, DC-DC_Converter_3_7V-5V.VIN, Rotary_Encoder.no_name_yet#2, Rotary_Encoder.no_name_yet#4, MS5611_Barometric_Pressure_Sensor.GND, Arduino_Nano_V3_0.GND, Buzzer_8_ohm.pin1, Nokia_5110_LCD_Module.GND
  5V: RTC_Module.5V, DC-DC_Converter_3_7V-5V.VOUT, R1.Pin_0, part_3.Pin_0, Arduino_Nano_V3_0.5V
  N2: RTC_Module.SQW, RTC_Module.SCL, MS5611_Barometric_Pressure_Sensor.SCL, Arduino_Nano_V3_0.A5
  N3: RTC_Module.SDA, MS5611_Barometric_Pressure_Sensor.SDA, Arduino_Nano_V3_0.A4
  N4: Mini_Slide_Switch.COM, DC-DC_Converter_3_7V-5V.GND
  N5: Rotary_Encoder.no_name_yet#1, part_3.Pin_1, Arduino_Nano_V3_0.D10
  N6: Rotary_Encoder.no_name_yet#3, R1.Pin_1, Arduino_Nano_V3_0.D11/MOSI
  N7: Rotary_Encoder.no_name_yet#5, part_2.Pin_1, Arduino_Nano_V3_0.D12/MISO
  VIN: MS5611_Barometric_Pressure_Sensor.VIN, part_2.Pin_0, Arduino_Nano_V3_0.3V3, Nokia_5110_LCD_Module.VCC
  N8: part.Pin_0, Arduino_Nano_V3_0.D9
  N9: part.Pin_1, Buzzer_8_ohm.pin2
  N10: Arduino_Nano_V3_0.D3, Nokia_5110_LCD_Module.LED
  N11: Arduino_Nano_V3_0.D4, Nokia_5110_LCD_Module.SCLK
  N12: Arduino_Nano_V3_0.D5, Nokia_5110_LCD_Module.DN(MODI)
  N13: Arduino_Nano_V3_0.D6, Nokia_5110_LCD_Module.D/C
  N14: Arduino_Nano_V3_0.D7, Nokia_5110_LCD_Module.RST
  N15: Arduino_Nano_V3_0.D8, Nokia_5110_LCD_Module.SCE

custom parts:
  Rotary Encoder with Knob: Rotary Encoder with 1/4" Shaft and Knob
  Nokia 5110 LCD basado en PCD8544: Módulo Nokia 5110 LCD basado en el controlador PCD8544. Versión de 8 pines (sólo entrada).
